# Fritzing sketch storegg (saved by Fritzing 0.9.3b)
perfboards: 2

parts:
  Raspberry_Pi_2 = Raspberry Pi 3 [part_number=RPI-3-V1.2]  # not connected
  S17 = Reed switch [package=THT]
  S18 = Reed switch [package=THT]
  S19 = Reed switch [package=THT]
  S20 = Reed switch [package=THT]
  S22 = Reed switch [package=THT]
  LED25 = smd LED [color="Yellow (585nm)" package="0603 [SMD]"]
  S21 = Reed switch [package=THT]
  R3 = Resistor [tolerance=±5% resistance=220 package=THT]
  LED27 = smd LED [color="Red (633nm)" package="0603 [SMD]"]  # not connected
  LED28 = smd LED [color="Red (633nm)" package="0603 [SMD]"]  # not connected
  LED29 = smd LED [color="Red (633nm)" package="0603 [SMD]"]  # not connected
  LED30 = smd LED [color="Green (565nm)" package="0603 [SMD]"]  # not connected
  LED31 = smd LED [color="Green (565nm)" package="0603 [SMD]"]  # not connected
  LED32 = smd LED [color="Yellow (585nm)" package="0603 [SMD]"]  # not connected
  LED33 = smd LED [color="Yellow (585nm)" package="0603 [SMD]"]  # not connected
  LED34 = smd LED [color="Yellow (585nm)" package="0603 [SMD]"]  # not connected
  J2 = double row male pin header, 20 pins [form="♂ (male)"]
  J3 = double row male pin header, 20 pins [form="♂ (male)"]
  R13 = Resistor [tolerance=±5% resistance=220 package=THT]  # not connected
  LED35 = smd LED [color="Yellow (585nm)" package="0603 [SMD]"]
  LED36 = smd LED [color="Yellow (585nm)" package="0603 [SMD]"]
  S23 = Toggle Switch [package=THT]
  S24 = Toggle Switch [package=THT]
  R14 = Resistor [tolerance=±5% resistance=220 package=THT]  # not connected
  R15 = Resistor [tolerance=±5% resistance=220 package=THT]  # not connected
  R16 = Resistor [tolerance=±5% resistance=220 package=THT]
  R17 = Resistor [tolerance=±5% resistance=220 package=THT]  # not connected
  R18 = Resistor [tolerance=±5% resistance=220 package=THT]  # not connected
  R19 = Resistor [tolerance=±5% resistance=220 package=THT]
  R20 = Resistor [tolerance=±5% resistance=220 package=THT]  # not connected
  R21 = Resistor [tolerance=±5% resistance=220 package=THT]  # not connected
  R22 = Resistor [tolerance=±5% resistance=220 package=THT]
  J6 = longpad pin header, 8 pins [form="long pad"]
  J5 = longpad pin header, 8 pins [form="long pad"]
  LED37 = smd LED [color="Yellow (585nm)" package="0603 [SMD]"]
  LED38 = smd LED [color="Yellow (585nm)" package="0603 [SMD]"]
  LED39 = smd LED [color="Yellow (585nm)" package="0603 [SMD]"]
  LED40 = smd LED [color="Yellow (585nm)" package="0603 [SMD]"]
  LED41 = smd LED [color="Yellow (585nm)" package="0603 [SMD]"]
  R23 = Resistor [tolerance=±5% resistance=220 package=THT]
  R25 = Resistor [tolerance=±5% resistance=220 package=THT]
  R26 = Resistor [tolerance=±5% resistance=220 package=THT]
  R27 = Resistor [tolerance=±5% resistance=220 package=THT]
  R28 = Resistor [tolerance=±5% resistance=220 package=THT]

nets:
  N1: S17.pin_1, LED25.anode
  N2: S18.pin_2, J2.pin2, J6.pin2, J5.pin2, LED39.anode
  N3: S19.pin_1, J3.pin2, J6.pin5, J5.pin5, LED40.anode
  N4: S20.pin_2, LED41.anode
  N5: S22.pin_1, S21.pin_2, J2.pin20, J6.pin1, J5.pin1
  N6: S22.pin_2, LED38.anode
  N7: LED25.cathode, R26.Pin_1
  N8: S21.pin_1, LED37.anode
  N9: R3.Pin_1, LED37.cathode
  N10: J2.pin1, R22.Pin_1
  N11: J2.pin13, LED35.cathode, S23.L1
  N12: J2.pin14, LED36.cathode, S24.L2
  N13: J2.pin15, J6.pin7, J5.pin7
  N14: J3.pin1, J6.pin6, J5.pin6
  N15: J3.pin3, J6.pin4, J5.pin4
  N16: J3.pin5, J6.pin3, J5.pin3
  N17: LED35.anode, R16.Pin_0
  N18: LED36.anode, R19.Pin_0
  N19: J6.pin8, J5.pin8, R23.Pin_1
  N20: LED38.cathode, R23.Pin_0
  N21: LED39.cathode, R28.Pin_1
  N22: LED40.cathode, R27.Pin_1
  N23: LED41.cathode, R25.Pin_1
